# Fritzing sketch tanklevel1 (saved by Fritzing 0.9.0b)
breadboards: 1

parts:
  Part1 = Arduino Nano (Rev3.0)
  NRF24L1 = NRF24L01
  S2 = Toggle Switch [package=THT]

nets:
  GND: Part1.GND, NRF24L1.GND, S2.GND
  N1: Part1.D9, NRF24L1.CE
  N2: Part1.D10, NRF24L1.CSN
  N3: Part1.D11/MOSI, NRF24L1.MOSI
  N4: Part1.D12/MISO, NRF24L1.MISO
  N5: Part1.A1, S2.Vout
  VCC: Part1.3V3, NRF24L1.VCC, S2.Vcc
  N6: Part1.D13/SCK, NRF24L1.SCK

custom parts:
  NRF24L01: NRF24L01 module
